# Fritzing sketch schematic (saved by Fritzing 0.9.3b)
breadboards: 2

parts:
  Part1 = Arduino Nano (Rev3.0) (ICSP)
  Grove1 = Grove OLED 128x96
  S1 = Pushbutton [package="[THT]"]
  S2 = Pushbutton [package="[THT]"]
  R1 = Resistor [tolerance=±5% resistance=1k package=THT]
  R2 = Resistor [tolerance=±5% resistance=1k package=THT]
  Part2 = Bluetooth HC-05 Macho

nets:
  GND: Part1.GND, Grove1.GND, R1.Pin_0, R2.Pin_0, Part2.GND
  N1: Part1.D5, S2.Pin_3, S2.Pin_4, R2.Pin_1
  N2: Part1.D6, S1.Pin_3, S1.Pin_4, R1.Pin_1
  N3: Part1.D9, Part2.Key
  N4: Part1.D10, Part2.TXD
  N5: Part1.D11/MOSI, Part2.RXD
  5V: Part1.5V, S1.Pin_1, S1.Pin_2, S2.Pin_1, S2.Pin_2, Part2.VCC
  N6: Part1.A5, Grove1.SCL
  N7: Part1.A4, Grove1.SDA
  3V3: Part1.3V3, Grove1.VCC

notes:
  This screen should be 128x64
